// Logisim project cache-test.circ as structural Verilog: 1 circuit, main circuit main
module main (
  input  [7:0] Address,
  output [7:0] Data
);

  wire clock_1_out, main_1_rom_read_enable;
  wire [5:0] main_1_rom_read_address;
  wire [31:0] rom_1_data;

  Clock clock_1 (.out(clock_1_out));
  LED led_1 (.in(main_1_rom_read_enable));
  cache_main main_1 (
    .address(Address), .data_out(Data), .ROM_read_address(main_1_rom_read_address),
    .ROM_read_enable(main_1_rom_read_enable), .ROM_data_in(rom_1_data), .read_enable(clock_1_out));
  ROM #(.addrWidth(6), .dataWidth(32)) rom_1 (
    .addr(main_1_rom_read_address), .data(rom_1_data), .sel(main_1_rom_read_enable));

  // Notes on the sheet:
  //   Reading ROM
  //   contents of rom_1 (hex, n*v repeats v):
  //   abcdef01 ca7f00d5 cafed00f f00dd00d b453b411 f007b411 5c00ba 12345678
endmodule
