// Logisim project cache.circ as structural Verilog: 2 circuits, main circuit cache-entry
module main (
  input  [7:0] address,
  input  read_enable,
  input  [31:0] ROM_data_in,
  output [7:0] data_out,
  output [5:0] ROM_read_address,
  output ROM_read_enable
);

  wire cache_entry_1_miss, cache_entry_2_miss, cache_entry_3_miss, cache_entry_4_miss, demultiplexer_1_out0,
       demultiplexer_1_out1, demultiplexer_1_out2, demultiplexer_1_out3, multiplexer_2_out;
  wire [31:0] cache_entry_1_data_out, cache_entry_2_data_out, cache_entry_3_data_out, cache_entry_4_data_out,
       multiplexer_1_out;

  Demultiplexer #(.select(2), .enable("false")) demultiplexer_1 (
    .out0(demultiplexer_1_out0), .out1(demultiplexer_1_out1), .out2(demultiplexer_1_out2),
    .out3(demultiplexer_1_out3), .in(read_enable), .sel(address[3:2]));
  and and_1 (ROM_read_enable, multiplexer_2_out, read_enable);
  cache_entry cache_entry_1 (
    .tag(address[7:4]), .clock(demultiplexer_1_out0), .data_out(cache_entry_1_data_out),
    .miss(cache_entry_1_miss), .data_in(ROM_data_in));
  cache_entry cache_entry_2 (
    .tag(address[7:4]), .clock(demultiplexer_1_out1), .data_out(cache_entry_2_data_out),
    .miss(cache_entry_2_miss), .data_in(ROM_data_in));
  cache_entry cache_entry_3 (
    .tag(address[7:4]), .clock(demultiplexer_1_out2), .data_out(cache_entry_3_data_out),
    .miss(cache_entry_3_miss), .data_in(ROM_data_in));
  cache_entry cache_entry_4 (
    .tag(address[7:4]), .clock(demultiplexer_1_out3), .data_out(cache_entry_4_data_out),
    .miss(cache_entry_4_miss), .data_in(ROM_data_in));
  Multiplexer #(.select(2), .width(32), .enable("false")) multiplexer_1 (
    .in0(cache_entry_1_data_out), .in1(cache_entry_2_data_out), .in2(cache_entry_3_data_out),
    .in3(cache_entry_4_data_out), .out(multiplexer_1_out), .sel(address[3:2]));
  Multiplexer #(.select(2), .enable("false")) multiplexer_2 (
    .in0(cache_entry_1_miss), .in1(cache_entry_2_miss), .in2(cache_entry_3_miss), .in3(cache_entry_4_miss),
    .out(multiplexer_2_out), .sel(address[3:2]));
  Multiplexer #(.select(2), .width(8), .enable("false")) multiplexer_3 (
    .in0(multiplexer_1_out[7:0]), .in1(multiplexer_1_out[15:8]), .in2(multiplexer_1_out[23:16]),
    .in3(multiplexer_1_out[31:24]), .out(data_out), .sel(address[1:0]));

  assign ROM_read_address = address[7:2];

  // Notes on the sheet:
  //   ROM_read_address: pull=down
  //   data_out: pull=down
  //   ROM_read_enable: pull=down
  //   index
  //   tag
  //   byte_offset
endmodule

module cache_entry (
  input  [31:0] data_in,
  input  [3:0] tag,
  input  clock,
  output [31:0] data_out,
  output miss
);

  wire and_1_out, comparator_1_eq, valid_q;
  wire [3:0] cache_tag_q;

  Register #(.width(1), .trigger("falling")) valid (.D(1'b1), .Q(valid_q), .clk(clock));  // open: en, clr
  Register #(.width(4), .trigger("falling")) cache_tag (.D(tag), .Q(cache_tag_q), .clk(clock));  // open: en, clr
  Register #(.width(32), .trigger("falling")) data (.D(data_in), .en(miss), .Q(data_out), .clk(clock));  // open: clr
  Comparator #(.width(4)) comparator_1 (.a(cache_tag_q), .b(tag), .eq(comparator_1_eq));  // open: gt, lt
  and and_1 (and_1_out, valid_q, comparator_1_eq);
  not not_1 (miss, and_1_out);
endmodule
